# Fritzing sketch esp8266-fritzing (saved by Fritzing 0.9.2b)
perfboards: 1

parts:
  Reset = Pushbutton [package="[THT]"]
  R2_Pullup = Resistor [tolerance=±5% resistance=47k package=THT]
  Temp_Connector = female pin header, 3 pins [form="♀ (female)"]
  R1_Pullup = Resistor [tolerance=±5% resistance=10k package=THT]
  ESP8266_lower = single row smd female pin header, 4 pins [form="♀ (female)"]
  ESP8266_upper = double row female pin header, 4 pins [form="♀ (female)"]
  Power_oben_GND_unten_VCC = female pin header, 2 pins [form="♀ (female)"]

nets:
  N1: Reset.Pin_1, Reset.Pin_2, Temp_Connector.pin2, ESP8266_lower.pin1, Power_oben_GND_unten_VCC.pin2
  N2: Reset.Pin_3, Reset.Pin_4, R1_Pullup.Pin_0, ESP8266_upper.pin2
  N3: R2_Pullup.Pin_0, Temp_Connector.pin1, R1_Pullup.Pin_1, ESP8266_upper.pin1, ESP8266_upper.pin3, Power_oben_GND_unten_VCC.pin1
  N4: R2_Pullup.Pin_1, Temp_Connector.pin3, ESP8266_lower.pin2
